// Logisim project smart_water_tank_logism.circ as structural Verilog: 1 circuit, main circuit main
module main (
  input  S0,
  input  S1,
  input  S2,
  input  S3,
  input  in_5,
  output PUMP,
  output L0,
  output C1,
  output FULL,
  output L1,
  output out_11,
  output ALARM,
  output C0,
  output out_14,
  output C1_2,
  output C0_2
);

  wire A_out, C_out, clock_1_out, d_ff_1_q, d_ff_2_q, d_ff_3_qn, D_out, F_out, not_1_out, not_4_out,
       undriven, xor_1_out;

  or or_1 (L0, S1, S3);
  or or_2 (L1, S2, S3);
  and F (F_out, F_out, not_1_out);
  D_Flip_Flop d_ff_1 (.D(L1), .clk(clock_1_out), .Q(d_ff_1_q), .reset(in_5));  // open: Qn, preset
  and and_1 (FULL, L0, L1);
  Clock clock_1 (.out(clock_1_out));
  not not_1 (not_1_out, d_ff_1_q);
  D_Flip_Flop d_ff_2 (.D(L0), .clk(clock_1_out), .Q(d_ff_2_q), .reset(in_5));  // open: Qn, preset
  or C (C_out, not_1_out, d_ff_2_q);
  _7_Segment_Display u_7_segment_display_1 (
    .f(clock_1_out), .a(A_out), .b(undriven), .e(F_out), .d(D_out), .c(D_out), .dp(C_out));  // open: g
  not not_2 (PUMP, FULL);
  not not_3 (F_out, d_ff_2_q);
  or A (A_out, d_ff_1_q, F_out);
  or D (D_out, d_ff_1_q, F_out);
  D_Flip_Flop d_ff_3 (.D(out_11), .clk(clock_1_out), .Q(C1), .Qn(d_ff_3_qn), .reset(in_5));  // open: preset
  D_Flip_Flop d_ff_4 (.D(out_14), .clk(clock_1_out), .Q(C0), .reset(in_5));  // open: Qn, preset
  not not_4 (not_4_out, C0);
  xor xor_1 (xor_1_out, d_ff_3_qn, C0);
  and and_2 (out_11, xor_1_out, FULL);
  buf and_3 (out_14, FULL);  // AND_Gate
  and and_4 (ALARM, C1, C0);

  // Notes on the sheet:
  //   FF1
  //   FF0
  //   B
  //   F= NOT (Q1) AND NOT (Q1)
  //   G=Q1
  //   8= NOT (Q1)
  //   B= 1
  //   C= NOT(Q1) OR Q0
  //   D=Q1 OR NOT (Q1)
  //   A= Q1 OR NOT QN
endmodule
